// Digital circuit core.dig as structural Verilog
module core (
  input  clk,
  input  start,
  input  reset,
  input  [7:0] block__id,
  input  [2:0] thread__count,
  input  program__mem__read__ready,
  input  [15:0] program__mem__read__data,
  input  [3:0] data__mem__read__ready,
  input  [31:0] data__mem__read__data,
  input  [3:0] data__mem__write__ready,
  output done,
  output program__mem__read__valid,
  output [7:0] program__mem__read__address,
  output [3:0] data__mem__read__valid,
  output [31:0] data__mem__read__address,
  output [3:0] data__mem__write__valid,
  output [31:0] data__mem__write__address,
  output [31:0] data__mem__write__data
);

  wire u_decoder_decoded_alu_output_mux, u_decoder_decoded_mem_read_enable,
       u_decoder_decoded_mem_write_enable, u_decoder_decoded_nzp_write_enable, u_decoder_decoded_pc_mux,
       u_decoder_decoded_reg_write_enable, u_decoder_decoded_ret;
  wire [1:0] u_decoder_decoded_alu_arithmetic_mux, u_decoder_decoded_reg_input_mux;
  wire [2:0] cs, u_decoder_decoded_nzp, u_fetcher_fetcher_state;
  wire [3:0] u_decoder_decoded_rd_address, u_decoder_decoded_rs_address, u_decoder_decoded_rt_address;
  wire [7:0] threads_1_lsu__state, u_decoder_decoded_immediate, u_scheduler_current_pc;
  wire [15:0] u_fetcher_instruction;
  wire [31:0] threads_1_next__pc;

  scheduler #(.applicationType("IVERILOG"), .iverilogOptions("-I ./src/"), .CodeFile("./src/scheduler.sv")) u_scheduler (
    .clk(clk), .reset(reset), .start(start), .decoded_mem_read_enable(u_decoder_decoded_mem_read_enable),
    .decoded_mem_write_enable(u_decoder_decoded_mem_write_enable), .decoded_ret(u_decoder_decoded_ret),
    .fetcher_state(u_fetcher_fetcher_state), .lsu_state(threads_1_lsu__state), .next_pc(threads_1_next__pc),
    .done(done), .core_state(cs), .current_pc(u_scheduler_current_pc));
  fetcher #(.applicationType("IVERILOG"), .iverilogOptions("-I ./src/"), .CodeFile("./src/fetcher.sv")) u_fetcher (
    .clk(clk), .reset(reset), .core_state(cs), .current_pc(u_scheduler_current_pc),
    .mem_read_ready(program__mem__read__ready), .mem_read_data(program__mem__read__data),
    .mem_read_valid(program__mem__read__valid), .mem_read_address(program__mem__read__address),
    .fetcher_state(u_fetcher_fetcher_state), .instruction(u_fetcher_instruction));
  decoder #(.applicationType("IVERILOG"), .iverilogOptions("-I ./src/"), .CodeFile("./src/decoder.sv")) u_decoder (
    .clk(clk), .reset(reset), .core_state(cs), .instruction(u_fetcher_instruction),
    .decoded_rd_address(u_decoder_decoded_rd_address), .decoded_rs_address(u_decoder_decoded_rs_address),
    .decoded_rt_address(u_decoder_decoded_rt_address), .decoded_nzp(u_decoder_decoded_nzp),
    .decoded_immediate(u_decoder_decoded_immediate),
    .decoded_reg_write_enable(u_decoder_decoded_reg_write_enable),
    .decoded_mem_read_enable(u_decoder_decoded_mem_read_enable),
    .decoded_mem_write_enable(u_decoder_decoded_mem_write_enable),
    .decoded_nzp_write_enable(u_decoder_decoded_nzp_write_enable),
    .decoded_reg_input_mux(u_decoder_decoded_reg_input_mux),
    .decoded_alu_arithmetic_mux(u_decoder_decoded_alu_arithmetic_mux),
    .decoded_alu_output_mux(u_decoder_decoded_alu_output_mux), .decoded_pc_mux(u_decoder_decoded_pc_mux),
    .decoded_ret(u_decoder_decoded_ret));
  threads threads_1 (
    .clk(clk), .reset(reset), .cs(cs), .decoded__rd__address(u_decoder_decoded_rd_address),
    .decoded__rs__address(u_decoder_decoded_rs_address), .decoded__rt__address(u_decoder_decoded_rt_address),
    .decoded__nzp(u_decoder_decoded_nzp), .decoded__immediate(u_decoder_decoded_immediate),
    .decoded__reg__write__enable(u_decoder_decoded_reg_write_enable),
    .decoded__mem__read__enable(u_decoder_decoded_mem_read_enable),
    .decoded__mem__write__enable(u_decoder_decoded_mem_write_enable),
    .decoded__nzp__write__enable(u_decoder_decoded_nzp_write_enable),
    .decoded__reg__input__mux(u_decoder_decoded_reg_input_mux),
    .decoded__alu__arithmetic__mux(u_decoder_decoded_alu_arithmetic_mux),
    .decoded__alu__output__mux(u_decoder_decoded_alu_output_mux),
    .decoded__pc__mux(u_decoder_decoded_pc_mux), .current__pc(u_scheduler_current_pc), .block__id(block__id),
    .data__mem__read__ready(data__mem__read__ready), .data__mem__read__data(data__mem__read__data),
    .data__mem__write__ready(data__mem__write__ready), .thread__count(thread__count),
    .data__mem__read__valid(data__mem__read__valid), .data__mem__read__address(data__mem__read__address),
    .data__mem__write__valid(data__mem__write__valid), .data__mem__write__address(data__mem__write__address),
    .data__mem__write__data(data__mem__write__data), .lsu__state(threads_1_lsu__state),
    .next__pc(threads_1_next__pc));
endmodule
