// Digital circuit gpu.dig as structural Verilog
module gpu (
  input  clk,
  input  reset,
  input  device__control__write__enable,
  input  [7:0] device__control__data,
  input  start,
  input  [3:0] data__mem__read__ready,
  input  [31:0] data__mem__read__data,
  input  [3:0] data__mem__write__ready,
  input  program__mem__read__ready,
  input  [15:0] program__mem__read__data,
  output done,
  output program__mem__read__valid,
  output [7:0] program__mem__read__address,
  output [3:0] data__mem__read__valid,
  output [31:0] data__mem__read__address,
  output [3:0] data__mem__write__valid,
  output [31:0] data__mem__write__address,
  output [31:0] data__mem__write__data
);

  wire done0, done1;
  wire [1:0] u_controllerProg_consumer_read_ready, u_dispatch_core_reset, u_dispatch_core_start, undriven_7;
  wire [2:0] u_dispatch_core_thread_count, u_dispatch_core_thread_count_2;
  wire [3:0] u_controllerData_consumer_write_ready, u_controllerData_consumer_write_ready_2, undriven_3,
       undriven_5, undriven_11, undriven_13;
  wire [7:0] u_controllerData_consumer_read_ready, u_dcr_thread_count, u_dispatch_core_block_id,
       u_dispatch_core_block_id_2, undriven_6, undriven_8;
  wire [15:0] u_controllerProg_consumer_read_data, u_controllerProg_consumer_read_data_2;
  wire [31:0] undriven, undriven_2, undriven_4, undriven_9, undriven_10, undriven_12;
  wire [63:0] u_controllerData_consumer_read_data;

  dispatch #(.applicationType("IVERILOG"), .iverilogOptions("-I ./src/"), .CodeFile("./src/dispatch.sv")) u_dispatch (
    .clk(clk), .reset(reset), .start(start), .thread_count(u_dcr_thread_count), .core_done({done1, done0}),
    .core_start(u_dispatch_core_start), .core_reset(u_dispatch_core_reset),
    .core_block_id({u_dispatch_core_block_id_2, u_dispatch_core_block_id}),
    .core_thread_count({u_dispatch_core_thread_count_2, u_dispatch_core_thread_count}), .done(done));
  dcr #(.applicationType("IVERILOG"), .iverilogOptions("-I ./src/"), .CodeFile("./src/dcr.sv")) u_dcr (
    .clk(clk), .reset(reset), .device_control_write_enable(device__control__write__enable),
    .device_control_data(device__control__data), .thread_count(u_dcr_thread_count));
  core core0 ();
  core core1 ();
  controllerData #(.applicationType("IVERILOG"), .iverilogOptions("-I ./src/"), .CodeFile("./src/controller-data.sv")) u_controllerData (
    .clk(clk), .reset(reset), .consumer_write_data({undriven_9, undriven}),
    .consumer_write_address({undriven_10, undriven_2}), .consumer_write_valid({undriven_11, undriven_3}),
    .consumer_read_address({undriven_12, undriven_4}), .consumer_read_valid({undriven_13, undriven_5}),
    .mem_read_ready(data__mem__read__ready), .mem_read_data(data__mem__read__data),
    .mem_write_ready(data__mem__write__ready), .consumer_read_ready(u_controllerData_consumer_read_ready),
    .consumer_read_data(u_controllerData_consumer_read_data),
    .consumer_write_ready({u_controllerData_consumer_write_ready_2, u_controllerData_consumer_write_ready}),
    .mem_read_valid(data__mem__read__valid), .mem_read_address(data__mem__read__address),
    .mem_write_valid(data__mem__write__valid), .mem_write_address(data__mem__write__address),
    .mem_write_data(data__mem__write__data));
  controllerProg #(.applicationType("IVERILOG"), .iverilogOptions("-I ./src/"), .CodeFile("./src/controller-program.sv")) u_controllerProg (
    .clk(clk), .reset(reset), .consumer_read_address({undriven_8, undriven_6}),
    .consumer_read_valid(undriven_7), .mem_read_ready(program__mem__read__ready),
    .mem_read_data(program__mem__read__data), .consumer_read_ready(u_controllerProg_consumer_read_ready),
    .consumer_read_data({u_controllerProg_consumer_read_data_2, u_controllerProg_consumer_read_data}),
    .mem_read_valid(program__mem__read__valid), .mem_read_address(program__mem__read__address));
endmodule
