// Digital circuit lsu.dig as structural Verilog
module lsu (
  input  clk,
  input  [2:0] in_9,
  input  in_10,
  input  [7:0] in_11,
  input  in_12,
  input  [7:0] in_13,
  input  [7:0] in_14,
  input  in_15,
  input  in_16,
  output out_1,
  output [7:0] out_2,
  output out_3,
  output [7:0] out_4,
  output [7:0] out_5,
  output [1:0] out_6,
  output [7:0] out_7
);

  lsu #(.applicationType("IVERILOG"), .iverilogOptions("-I /Users/markren/LocalFiles/tiny-gpu/src/digital"), .CodeFile("/Users/markren/LocalFiles/tiny-gpu/src/digital/lsu.sv")) u_lsu (
    .clk(clk), .reset(in_15), .enable(in_16), .core_state(in_9), .decoded_mem_read_enable(1'b0),
    .decoded_mem_write_enable(1'b1), .rs(in_13), .rt(in_14), .mem_read_ready(in_10), .mem_read_data(in_11),
    .mem_write_ready(in_12), .mem_read_valid(out_1), .mem_read_address(out_2), .mem_write_valid(out_3),
    .mem_write_address(out_4), .mem_write_data(out_5), .lsu_state(out_6), .lsu_out(out_7));
endmodule
