// Digital circuit pc.dig as structural Verilog
module pc (
  input  clk,
  input  reset,
  input  [2:0] cs,
  input  en,
  input  [2:0] in_5,
  input  in_6,
  input  in_7,
  input  [7:0] in_8,
  input  [7:0] in_10,
  input  [7:0] in_11,
  output [7:0] next__pc
);

  pc #(.applicationType("IVERILOG"), .iverilogOptions("-I /Users/markren/LocalFiles/tiny-gpu/src/digital"), .CodeFile("/Users/markren/LocalFiles/tiny-gpu/src/digital/pc.sv")) u_pc (
    .clk(clk), .reset(reset), .enable(en), .core_state(cs), .decoded_nzp(in_5), .decoded_immediate(in_10),
    .decoded_nzp_write_enable(in_6), .decoded_pc_mux(in_7), .alu_out(in_11), .current_pc(in_8),
    .next_pc(next__pc));
endmodule
