// Digital circuit registers.dig as structural Verilog
module registers (
  input  reset,
  input  clk,
  input  en,
  input  [7:0] in_4,
  input  [2:0] in_5,
  input  [3:0] in_6,
  input  [3:0] in_7,
  input  [3:0] in_8,
  input  in_9,
  input  [1:0] in_10,
  input  [7:0] in_11,
  input  [7:0] in_12,
  input  [7:0] in_13,
  output [7:0] out_14,
  output [7:0] out_15
);

  registers #(.applicationType("IVERILOG"), .iverilogOptions("-I /Users/markren/LocalFiles/tiny-gpu/src/digital"), .CodeFile("/Users/markren/LocalFiles/tiny-gpu/src/digital/registers.sv")) u_registers (
    .clk(clk), .reset(reset), .enable(en), .block_id(in_4), .core_state(in_5), .decoded_rd_address(in_6),
    .decoded_rs_address(in_7), .decoded_rt_address(in_8), .decoded_reg_write_enable(in_9),
    .decoded_reg_input_mux(in_10), .decoded_immediate(in_11), .alu_out(in_12), .lsu_out(in_13), .rs(out_14),
    .rt(out_15));
endmodule
