// Digital circuit splitter40-10.dig as structural Verilog
module splitter40_10 (
  input  [39:0] in40,
  input  [1:0] id,
  output rr,
  output [7:0] rd,
  output wr
);

  Multiplexer #(.Selector_Bits(2), .Bits(8)) multiplexer_1 (
    .sel(id), .in_0(in40[11:4]), .in_1(in40[19:12]), .in_2(in40[27:20]), .in_3(in40[35:28]), .out(rd));
  Multiplexer #(.Selector_Bits(2)) multiplexer_2 (
    .sel(id), .in_0(in40[0]), .in_1(in40[1]), .in_2(in40[2]), .in_3(in40[3]), .out(rr));
  Multiplexer #(.Selector_Bits(2)) multiplexer_3 (
    .sel(id), .in_0(in40[36]), .in_1(in40[37]), .in_2(in40[38]), .in_3(in40[39]), .out(wr));
endmodule
