// Digital circuit thread.dig as structural Verilog
module thread (
  input  clk,
  input  reset,
  input  [2:0] cs,
  input  en,
  input  [3:0] decoded__rd__address,
  input  [3:0] decoded__rs__address,
  input  [3:0] decoded__rt__address,
  input  [2:0] decoded__nzp,
  input  [7:0] decoded__immediate,
  input  decoded__reg__write__enable,
  input  decoded__mem__read__enable,
  input  decoded__mem__write__enable,
  input  decoded__nzp__write__enable,
  input  [1:0] decoded__reg__input__mux,
  input  [1:0] decoded__alu__arithmetic__mux,
  input  decoded__alu__output__mux,
  input  decoded__pc__mux,
  input  [7:0] block__id,
  input  [7:0] current__pc,
  input  mem__read__ready,
  input  [7:0] mem__read__data,
  input  mem__write__ready,
  output mem__read__valid,
  output [7:0] mem__read__address,
  output mem__write__valid,
  output [7:0] mem__write__address,
  output [7:0] mem__write__data,
  output [1:0] lsu__state,
  output [7:0] next__pc
);

  wire [7:0] u_alu_alu_out, u_lsu_lsu_out, u_registers_rs, u_registers_rt;

  registers #(.applicationType("IVERILOG"), .iverilogOptions("-I ./src/"), .CodeFile("./src/registers.sv")) u_registers (
    .clk(clk), .reset(reset), .enable(en), .block_id(block__id), .core_state(cs),
    .decoded_rd_address(decoded__rd__address), .decoded_rs_address(decoded__rs__address),
    .decoded_rt_address(decoded__rt__address), .decoded_reg_write_enable(decoded__reg__write__enable),
    .decoded_reg_input_mux(decoded__reg__input__mux), .decoded_immediate(decoded__immediate),
    .alu_out(u_alu_alu_out), .lsu_out(u_lsu_lsu_out), .rs(u_registers_rs), .rt(u_registers_rt));
  pc #(.applicationType("IVERILOG"), .iverilogOptions("-I ./src/"), .CodeFile("./src/pc.sv")) u_pc (
    .clk(clk), .reset(reset), .enable(en), .core_state(cs), .decoded_nzp(decoded__nzp),
    .decoded_immediate(decoded__immediate), .decoded_nzp_write_enable(decoded__nzp__write__enable),
    .decoded_pc_mux(decoded__pc__mux), .alu_out(u_alu_alu_out), .current_pc(current__pc), .next_pc(next__pc));
  alu #(.applicationType("IVERILOG"), .iverilogOptions("-I ./src/"), .CodeFile("./src/alu.sv")) u_alu (
    .clk(clk), .reset(reset), .enable(en), .core_state(cs),
    .decoded_alu_arithmetic_mux(decoded__alu__arithmetic__mux),
    .decoded_alu_output_mux(decoded__alu__output__mux), .rs(u_registers_rs), .rt(u_registers_rt),
    .alu_out(u_alu_alu_out));
  lsu #(.applicationType("IVERILOG"), .iverilogOptions("-I ./src/"), .CodeFile("./src/lsu.sv")) u_lsu (
    .clk(clk), .reset(reset), .enable(en), .core_state(cs),
    .decoded_mem_read_enable(decoded__mem__read__enable),
    .decoded_mem_write_enable(decoded__mem__write__enable), .rs(u_registers_rs), .rt(u_registers_rt),
    .mem_read_ready(mem__read__ready), .mem_read_data(mem__read__data), .mem_write_ready(mem__write__ready),
    .mem_read_valid(mem__read__valid), .mem_read_address(mem__read__address),
    .mem_write_valid(mem__write__valid), .mem_write_address(mem__write__address),
    .mem_write_data(mem__write__data), .lsu_state(lsu__state), .lsu_out(u_lsu_lsu_out));
endmodule
