// Digital circuit threads.dig as structural Verilog
module threads (
  input  clk,
  input  reset,
  input  [2:0] cs,
  input  [3:0] decoded__rd__address,
  input  [3:0] decoded__rs__address,
  input  [3:0] decoded__rt__address,
  input  [2:0] decoded__nzp,
  input  [7:0] decoded__immediate,
  input  decoded__reg__write__enable,
  input  decoded__mem__read__enable,
  input  decoded__mem__write__enable,
  input  decoded__nzp__write__enable,
  input  [1:0] decoded__reg__input__mux,
  input  [1:0] decoded__alu__arithmetic__mux,
  input  decoded__alu__output__mux,
  input  decoded__pc__mux,
  input  [7:0] current__pc,
  input  [7:0] block__id,
  input  [3:0] data__mem__read__ready,
  input  [31:0] data__mem__read__data,
  input  [3:0] data__mem__write__ready,
  input  [2:0] thread__count,
  output [3:0] data__mem__read__valid,
  output [31:0] data__mem__read__address,
  output [3:0] data__mem__write__valid,
  output [31:0] data__mem__write__address,
  output [31:0] data__mem__write__data,
  output [7:0] lsu__state,
  output [31:0] next__pc
);

  wire comparator_1_lt, comparator_2_lt, comparator_3_lt, comparator_4_lt, splitter40_10_1_rr,
       splitter40_10_1_wr, splitter40_10_2_rr, splitter40_10_2_wr, splitter40_10_3_rr, splitter40_10_3_wr,
       splitter40_10_4_rr, splitter40_10_4_wr;
  wire [1:0] thread0_lsu__state, thread1_lsu__state, thread2_lsu__state, thread3_lsu__state;
  wire [7:0] splitter40_10_1_rd, splitter40_10_2_rd, splitter40_10_3_rd, splitter40_10_4_rd,
       thread0_mem__read__address, thread0_mem__write__address, thread0_mem__write__data, thread0_next__pc,
       thread1_mem__read__address, thread1_mem__write__address, thread1_mem__write__data, thread1_next__pc,
       thread2_mem__read__address, thread2_mem__write__address, thread2_mem__write__data, thread2_next__pc,
       thread3_mem__read__address, thread3_mem__write__address, thread3_mem__write__data, thread3_next__pc;
  wire [9:0] thread0_mem__write__valid, thread1_mem__write__valid, thread2_mem__read__valid,
       thread3_mem__read__valid;

  Comparator #(.Bits(3)) comparator_1 (.a(3'b000), .b(thread__count), .lt(comparator_1_lt));  // open: gt, eq
  Comparator #(.Bits(3)) comparator_2 (.a(3'b010), .b(thread__count), .lt(comparator_2_lt));  // open: gt, eq
  splitter40_10 splitter40_10_1 (
    .in40({data__mem__write__ready, data__mem__read__data, data__mem__read__ready}), .id(2'b00),
    .rr(splitter40_10_1_rr), .rd(splitter40_10_1_rd), .wr(splitter40_10_1_wr));
  splitter40_10 splitter40_10_2 (
    .in40({data__mem__write__ready, data__mem__read__data, data__mem__read__ready}), .id(2'b10),
    .rr(splitter40_10_2_rr), .rd(splitter40_10_2_rd), .wr(splitter40_10_2_wr));
  thread thread0 (
    .clk(clk), .reset(reset), .cs(cs), .en(comparator_1_lt), .decoded__rd__address(decoded__rd__address),
    .decoded__rs__address(decoded__rs__address), .decoded__rt__address(decoded__rt__address),
    .decoded__nzp(decoded__nzp), .decoded__immediate(decoded__immediate),
    .decoded__reg__write__enable(decoded__reg__write__enable),
    .decoded__mem__read__enable(decoded__mem__read__enable),
    .decoded__mem__write__enable(decoded__mem__write__enable),
    .decoded__nzp__write__enable(decoded__nzp__write__enable),
    .decoded__reg__input__mux(decoded__reg__input__mux),
    .decoded__alu__arithmetic__mux(decoded__alu__arithmetic__mux),
    .decoded__alu__output__mux(decoded__alu__output__mux), .decoded__pc__mux(decoded__pc__mux),
    .block__id(block__id), .current__pc(current__pc), .mem__read__ready(splitter40_10_1_rr),
    .mem__read__data(splitter40_10_1_rd), .mem__write__ready(splitter40_10_1_wr),
    .mem__read__valid(thread0_mem__write__valid[0]), .mem__read__address(thread0_mem__read__address),
    .mem__write__valid(thread0_mem__write__valid[9]), .mem__write__address(thread0_mem__write__address),
    .mem__write__data(thread0_mem__write__data), .lsu__state(thread0_lsu__state), .next__pc(thread0_next__pc));
  thread thread2 (
    .clk(clk), .reset(reset), .cs(cs), .en(comparator_2_lt), .decoded__rd__address(decoded__rd__address),
    .decoded__rs__address(decoded__rs__address), .decoded__rt__address(decoded__rt__address),
    .decoded__nzp(decoded__nzp), .decoded__immediate(decoded__immediate),
    .decoded__reg__write__enable(decoded__reg__write__enable),
    .decoded__mem__read__enable(decoded__mem__read__enable),
    .decoded__mem__write__enable(decoded__mem__write__enable),
    .decoded__nzp__write__enable(decoded__nzp__write__enable),
    .decoded__reg__input__mux(decoded__reg__input__mux),
    .decoded__alu__arithmetic__mux(decoded__alu__arithmetic__mux),
    .decoded__alu__output__mux(decoded__alu__output__mux), .decoded__pc__mux(decoded__pc__mux),
    .block__id(block__id), .current__pc(current__pc), .mem__read__ready(splitter40_10_2_rr),
    .mem__read__data(splitter40_10_2_rd), .mem__write__ready(splitter40_10_2_wr),
    .mem__read__valid(thread2_mem__read__valid[0]), .mem__read__address(thread2_mem__read__address),
    .mem__write__valid(thread2_mem__read__valid[9]), .mem__write__address(thread2_mem__write__address),
    .mem__write__data(thread2_mem__write__data), .lsu__state(thread2_lsu__state), .next__pc(thread2_next__pc));
  Comparator #(.Bits(3)) comparator_3 (.a(3'b001), .b(thread__count), .lt(comparator_3_lt));  // open: gt, eq
  Comparator #(.Bits(3)) comparator_4 (.a(3'b011), .b(thread__count), .lt(comparator_4_lt));  // open: gt, eq
  splitter40_10 splitter40_10_3 (
    .in40({data__mem__write__ready, data__mem__read__data, data__mem__read__ready}), .id(2'b01),
    .rr(splitter40_10_3_rr), .rd(splitter40_10_3_rd), .wr(splitter40_10_3_wr));
  splitter40_10 splitter40_10_4 (
    .in40({data__mem__write__ready, data__mem__read__data, data__mem__read__ready}), .id(2'b11),
    .rr(splitter40_10_4_rr), .rd(splitter40_10_4_rd), .wr(splitter40_10_4_wr));
  thread thread1 (
    .clk(clk), .reset(reset), .cs(cs), .en(comparator_3_lt), .decoded__rd__address(decoded__rd__address),
    .decoded__rs__address(decoded__rs__address), .decoded__rt__address(decoded__rt__address),
    .decoded__nzp(decoded__nzp), .decoded__immediate(decoded__immediate),
    .decoded__reg__write__enable(decoded__reg__write__enable),
    .decoded__mem__read__enable(decoded__mem__read__enable),
    .decoded__mem__write__enable(decoded__mem__write__enable),
    .decoded__nzp__write__enable(decoded__nzp__write__enable),
    .decoded__reg__input__mux(decoded__reg__input__mux),
    .decoded__alu__arithmetic__mux(decoded__alu__arithmetic__mux),
    .decoded__alu__output__mux(decoded__alu__output__mux), .decoded__pc__mux(decoded__pc__mux),
    .block__id(block__id), .current__pc(current__pc), .mem__read__ready(splitter40_10_3_rr),
    .mem__read__data(splitter40_10_3_rd), .mem__write__ready(splitter40_10_3_wr),
    .mem__read__valid(thread1_mem__write__valid[0]), .mem__read__address(thread1_mem__read__address),
    .mem__write__valid(thread1_mem__write__valid[9]), .mem__write__address(thread1_mem__write__address),
    .mem__write__data(thread1_mem__write__data), .lsu__state(thread1_lsu__state), .next__pc(thread1_next__pc));
  thread thread3 (
    .clk(clk), .reset(reset), .cs(cs), .en(comparator_4_lt), .decoded__rd__address(decoded__rd__address),
    .decoded__rs__address(decoded__rs__address), .decoded__rt__address(decoded__rt__address),
    .decoded__nzp(decoded__nzp), .decoded__immediate(decoded__immediate),
    .decoded__reg__write__enable(decoded__reg__write__enable),
    .decoded__mem__read__enable(decoded__mem__read__enable),
    .decoded__mem__write__enable(decoded__mem__write__enable),
    .decoded__nzp__write__enable(decoded__nzp__write__enable),
    .decoded__reg__input__mux(decoded__reg__input__mux),
    .decoded__alu__arithmetic__mux(decoded__alu__arithmetic__mux),
    .decoded__alu__output__mux(decoded__alu__output__mux), .decoded__pc__mux(decoded__pc__mux),
    .block__id(block__id), .current__pc(current__pc), .mem__read__ready(splitter40_10_4_rr),
    .mem__read__data(splitter40_10_4_rd), .mem__write__ready(splitter40_10_4_wr),
    .mem__read__valid(thread3_mem__read__valid[0]), .mem__read__address(thread3_mem__read__address),
    .mem__write__valid(thread3_mem__read__valid[9]), .mem__write__address(thread3_mem__write__address),
    .mem__write__data(thread3_mem__write__data), .lsu__state(thread3_lsu__state), .next__pc(thread3_next__pc));
  splitter144 #(.applicationType("IVERILOG"), .iverilogOptions("-I ./src/"), .CodeFile("./src/splitter144.sv")) u_splitter144 (
    .in0({thread0_next__pc, thread0_lsu__state, thread0_mem__write__data, thread0_mem__write__address, thread0_mem__write__valid[9], thread0_mem__read__address, thread0_mem__write__valid[0]}),
    .in1({thread1_next__pc, thread1_lsu__state, thread1_mem__write__data, thread1_mem__write__address, thread1_mem__write__valid[9], thread1_mem__read__address, thread1_mem__write__valid[0]}),
    .in2({thread2_next__pc, thread2_lsu__state, thread2_mem__write__data, thread2_mem__write__address, thread2_mem__read__valid[9], thread2_mem__read__address, thread2_mem__read__valid[0]}),
    .in3({thread3_next__pc, thread3_lsu__state, thread3_mem__write__data, thread3_mem__write__address, thread3_mem__read__valid[9], thread3_mem__read__address, thread3_mem__read__valid[0]}),
    .out0(data__mem__read__valid), .out1(data__mem__read__address), .out2(data__mem__write__valid),
    .out3(data__mem__write__address), .out4(data__mem__write__data), .out5(lsu__state), .out6(next__pc));
endmodule
